// Logisim project Laborator.circ as structural Verilog: 7 circuits, main circuit main
module main (
  input  S0,
  input  S1,
  input  Serial_Input,
  input  I0,
  input  I1,
  input  I2,
  input  Serial_Input_2,
  input  I3,
  output A0,
  output A1,
  output A2,
  output A3
);

  wire Clock_out, mux_4x1_1_out_7, mux_4x1_2_out_7, mux_4x1_3_out_7, mux_4x1_4_out_7;

  Clock Clock (.out(Clock_out));
  MUX_4x1 mux_4x1_1 (.S0(S0), .S1(S1), .I0(A0), .I1(Serial_Input), .I2(A1), .I3(I0), .out_7(mux_4x1_1_out_7));
  MUX_4x1 mux_4x1_2 (.S0(S0), .S1(S1), .I0(A1), .I1(A0), .I2(A2), .I3(I1), .out_7(mux_4x1_2_out_7));
  MUX_4x1 mux_4x1_3 (.S0(S0), .S1(S1), .I0(A2), .I1(A1), .I2(A3), .I3(I2), .out_7(mux_4x1_3_out_7));
  MUX_4x1 mux_4x1_4 (.S0(S0), .S1(S1), .I0(A3), .I1(A2), .I2(Serial_Input_2), .I3(I3), .out_7(mux_4x1_4_out_7));
  D d_1 (.D(mux_4x1_4_out_7), .Clock(Clock_out), .Q(A3));  // open: Q_prime
  D d_2 (.D(mux_4x1_1_out_7), .Clock(Clock_out), .Q(A0));  // open: Q_prime
  D d_3 (.D(mux_4x1_2_out_7), .Clock(Clock_out), .Q(A1));  // open: Q_prime
  D d_4 (.D(mux_4x1_3_out_7), .Clock(Clock_out), .Q(A2));  // open: Q_prime

  // Notes on the sheet:
  //   Registru de deplasare cu incarcare paralela
endmodule

module SR (
  input  S,
  input  Clock,
  input  R,
  output out_4,
  output out_5
);

  wire and_1_out, and_2_out;

  and and_1 (and_1_out, S, Clock);
  and and_2 (and_2_out, Clock, R);
  SR_asincron sr_asincron_1 (.S(and_1_out), .R(and_2_out), .Q(out_4), .Q_prime(out_5));
endmodule

module D (
  input  D,
  input  Clock,
  output Q,
  output Q_prime
);

  wire not_1_out;

  not not_1 (not_1_out, D);
  SR sr_1 (.S(D), .Clock(Clock), .R(not_1_out), .out_4(Q), .out_5(Q_prime));
endmodule

module JK (
  input  J,
  input  Clock,
  input  K,
  output Q,
  output Q_prime
);

  wire and_1_out, and_2_out;

  and and_1 (and_1_out, Q_prime, J);
  and and_2 (and_2_out, K, Q);
  SR sr_1 (.S(and_1_out), .Clock(Clock), .R(and_2_out), .out_4(Q), .out_5(Q_prime));
endmodule

module MUX_4x1 (
  input  S0,
  input  S1,
  input  I0,
  input  I1,
  input  I2,
  input  I3,
  output out_7
);

  wire and_1_out, and_2_out, and_3_out, and_4_out, not_1_out, not_2_out;

  not not_1 (not_1_out, S0);
  not not_2 (not_2_out, S1);
  and and_1 (and_1_out, I0, not_1_out, not_2_out);
  and and_2 (and_2_out, I1, S0, not_2_out);
  and and_3 (and_3_out, I2, S1, not_1_out);
  and and_4 (and_4_out, I3, S1, S0);
  or or_1 (out_7, and_1_out, and_2_out, and_3_out, and_4_out);
endmodule

module T (
  input  T,
  input  Clock,
  output Q,
  output Q_prime
);

  wire not_1_out;

  not not_1 (not_1_out, T);
  JK jk_1 (.J(T), .Clock(Clock), .K(not_1_out), .Q(Q), .Q_prime(Q_prime));
endmodule

module SR_asincron (
  input  S,
  input  R,
  output Q,
  output Q_prime
);

  nor nor_1 (Q, R, Q_prime);
  nor nor_2 (Q_prime, Q, S);
endmodule
