// Logisim project capitolul 2.circ as structural Verilog: 3 circuits, main circuit main
module main (
  input  a,
  input  b,
  input  a_2,
  input  b_2,
  input  c,
  input  c_2,
  input  a_3,
  input  a1,
  input  b_3,
  input  a2,
  input  a3,
  input  a_4,
  input  in_13,
  input  b_4,
  input  in_15,
  input  c_3,
  input  in_17,
  input  a_5,
  input  b_5,
  input  a_6,
  input  in_21,
  input  in_22,
  output M,
  output P,
  output d2,
  output T1,
  output d1,
  output s1,
  output d0,
  output T2,
  output A_7,
  output B_6,
  output s2,
  output C_4,
  output ab,
  output a_prime,
  output out_37
);

  wire and_2_out, and_3_out, nand_1_out, nand_3_out, nand_4_out, not_1_out, semisumator_1_out_3,
       semisumator_1_out_4, semisumator_2_out_3, xor_1_out;

  not not_1 (not_1_out, a3);
  xor xor_1 (xor_1_out, a, b);
  and and_1 (d2, a3, not_1_out);
  Semisumator semisumator_1 (.in_1(a_4), .in_2(b_4), .out_3(semisumator_1_out_3), .out_4(semisumator_1_out_4));
  nand nand_1 (nand_1_out, a_5, b_5);
  nand nand_2 (a_prime, a_6, a_6);
  nand nand_3 (nand_3_out, in_21, in_21);
  nand nand_4 (nand_4_out, in_22, in_22);
  and and_2 (and_2_out, a, b);
  and and_3 (and_3_out, xor_1_out, c);
  Semisumator semisumator_2 (.in_1(semisumator_1_out_4), .in_2(c_3), .out_3(semisumator_2_out_3), .out_4(s2));
  nand nand_5 (ab, nand_1_out, nand_1_out);
  nand nand_6 (out_37, nand_3_out, nand_4_out);
  or or_1 (T2, semisumator_1_out_3, semisumator_2_out_3);
  or or_2 (M, and_3_out, and_2_out);
  Semisumator semisumator_3 (.in_1(a_3), .in_2(b_3), .out_3(T1), .out_4(s1));
  Sumator_complet sumator_complet_1 (.a(in_13), .b(in_15), .c(in_17), .S(A_7), .C0(B_6));
  not not_2 (C_4, in_15);
  NotExactlyOne xnor_1 (.out(P), .in0(a_2), .in2(b_2), .in4(c_2));

  assign d0 = a2;
  assign d1 = a1;

  // Notes on the sheet:
  //   Problema 3
  //   Prolblema 1
  //   Problema 4
  //   Problema 6
  //   Problema 5
  //   Problema 2
  //   Problema 4
endmodule

// +|2
module Semisumator (
  input  in_1,
  input  in_2,
  output out_3,
  output out_4
);

  xor xor_1 (out_3, in_1, in_2);
  and and_1 (out_4, in_1, in_2);
endmodule

module Sumator_complet (
  input  a,
  input  b,
  input  c,
  output S,
  output C0
);

  wire and_1_out, and_2_out, xor_1_out;

  xor xor_1 (xor_1_out, a, b);
  xor xor_2 (S, xor_1_out, c);
  and and_1 (and_1_out, c, xor_1_out);
  and and_2 (and_2_out, a, b);
  or or_1 (C0, and_1_out, and_2_out);
endmodule
