// Logisim project capitolul 3.circ as structural Verilog: 4 circuits, main circuit main
module main (
  input  a,
  input  b,
  input  c,
  input  a_2,
  input  b_2,
  input  D0,
  input  D1,
  input  x,
  input  y,
  input  z,
  input  C0,
  input  C1,
  input  C2,
  input  B_3,
  input  I0,
  input  A_3,
  input  I1,
  input  I2,
  input  S,
  input  I3,
  input  I4,
  input  I5,
  input  I6,
  input  I7,
  input  S3,
  input  S2,
  input  S1,
  input  S0,
  input  I,
  input  I8,
  input  I9,
  input  I10,
  input  I11,
  input  I12,
  input  S0_2,
  input  S1_2,
  input  I13,
  input  I14,
  input  I15,
  output a_prime_b_prime_c_prime,
  output a_prime_b_prime_c,
  output a_prime_bc_prime,
  output a_prime_b_prime,
  output a_prime_bc,
  output a_prime_b,
  output ab_prime,
  output ab_prime_b_prime,
  output ab_prime_c,
  output abc_prime,
  output ab,
  output abc,
  output out_52,
  output f_C_D,
  output Y_2,
  output Y_3,
  output O0,
  output O1,
  output O2,
  output O3
);

  wire and_1_out, multiplexor_8x1_2_out_12, not_1_out, not_2_out, not_3_out, not_4_out, not_5_out, or_1_out,
       xnor_1_out, xor_1_out;

  not not_1 (not_1_out, a_2);
  not not_2 (not_2_out, b_2);
  Multiplexer multiplexer_1 (.in0(B_3), .in1(A_3), .out(Y_2), .sel(S));  // open: en
  DMUX dmux_1 (.I(I), .S0(S1_2), .S1(S0_2), .IS0S1(O0), .IS0S1_O1(O1), .IS0S1_O2(O2), .IS0S1_O3(O3));
  nor nor_1 (a_prime_b_prime, not_1_out, not_2_out);
  nor nor_2 (a_prime_b, not_1_out, b_2);
  nor nor_3 (ab_prime, a_2, not_2_out);
  nor nor_4 (ab, a_2, b_2);
  Multiplexor_8x1 multiplexor_8x1_1 (
    .in_1(1'b1), .in_2(1'b0), .in_3(1'b0), .in_4(1'b1), .in_5(1'b1), .in_6(1'b0), .in_7(1'b1), .in_8(1'b1),
    .out_12(out_52), .in_9(x), .in_10(y), .in_11(z));
  not not_3 (not_3_out, a);
  Multiplexor_8x1 multiplexor_8x1_2 (
    .in_1(I15), .in_2(I14), .in_3(I13), .in_4(I12), .in_5(I11), .in_6(I10), .in_7(I9), .in_8(I8),
    .out_12(multiplexor_8x1_2_out_12), .in_9(S1), .in_10(S2), .in_11(S3));
  Dec_2x4 dec_2x4_1 (
    .a(not_3_out), .b(b), .ENABLE(c), .ab(a_prime_b_prime_c_prime), .ab_prime(a_prime_b_prime_c),
    .a_prime_b(a_prime_bc_prime), .a_prime_b_prime(a_prime_bc));
  Dec_2x4 dec_2x4_2 (
    .a(a), .b(b), .ENABLE(c), .ab(ab_prime_b_prime), .ab_prime(ab_prime_c), .a_prime_b(abc_prime),
    .a_prime_b_prime(abc));
  not not_4 (not_4_out, D0);
  not not_5 (not_5_out, D1);
  and and_1 (and_1_out, D1, D0);
  or or_1 (or_1_out, D1, D0);
  xor xor_1 (xor_1_out, D1, D0);
  xnor xnor_1 (xnor_1_out, D1, D0);
  Multiplexor_8x1 multiplexor_8x1_3 (
    .in_1(I0), .in_2(I1), .in_3(I2), .in_4(I3), .in_5(I4), .in_6(I5), .in_7(I6), .in_8(I7),
    .out_12(multiplexor_8x1_2_out_12), .in_9(S3), .in_10(S2), .in_11(S1));
  Multiplexer multiplexer_2 (
    .in0(multiplexor_8x1_2_out_12), .in1(multiplexor_8x1_2_out_12), .out(Y_3), .sel(S0));  // open: en
  Multiplexor_8x1 multiplexor_8x1_4 (
    .in_1(D0), .in_2(not_4_out), .in_3(D1), .in_4(not_5_out), .in_5(and_1_out), .in_6(or_1_out),
    .in_7(xor_1_out), .in_8(xnor_1_out), .out_12(f_C_D), .in_9(C0), .in_10(C1), .in_11(C2));

  // Notes on the sheet:
  //   a
  //   I0
  //   I1
  //   I2
  //   I3
  //   I4
  //   I5
  //   I6
  //   I7
  //   Problema 1
  //   b
  //   b'
  //   a'
  //   Problema 5
  //   Problema 7
  //   Problema 3
  //   Problema 6
  //   Problema 2
  //   Problema 4
endmodule

module Dec_2x4 (
  input  a,
  input  b,
  input  ENABLE,
  output ab,
  output ab_prime,
  output a_prime_b,
  output a_prime_b_prime
);

  wire not_1_out, not_2_out;

  not not_1 (not_1_out, a);
  not not_2 (not_2_out, b);
  and and_1 (ab, a, b, ENABLE);
  and and_2 (ab_prime, a, not_2_out, ENABLE);
  and and_3 (a_prime_b, not_1_out, b, ENABLE);
  and and_4 (a_prime_b_prime, not_1_out, not_2_out, ENABLE);

  // Notes on the sheet:
  //   a
  //   a'
  //   b
  //   b'
endmodule

// MUX 8x1
module Multiplexor_8x1 (
  input  in_1,
  input  in_2,
  input  in_3,
  input  in_4,
  input  in_5,
  input  in_6,
  input  in_7,
  input  in_8,
  input  in_9,
  input  in_10,
  input  in_11,
  output out_12
);

  wire and_1_out, and_2_out, and_3_out, and_4_out, and_5_out, and_6_out, and_7_out, and_8_out, not_1_out,
       not_2_out, not_3_out;

  not not_1 (not_1_out, in_9);
  not not_2 (not_2_out, in_10);
  not not_3 (not_3_out, in_11);
  and and_1 (and_1_out, in_1, not_1_out, not_2_out, not_3_out);
  and and_2 (and_2_out, in_2, not_1_out, not_2_out, in_11);
  and and_3 (and_3_out, in_3, not_1_out, in_10, not_3_out);
  and and_4 (and_4_out, in_4, not_1_out, in_10, in_11);
  and and_5 (and_5_out, in_5, in_9, not_2_out, not_3_out);
  and and_6 (and_6_out, in_6, in_9, not_2_out, in_11);
  and and_7 (and_7_out, in_7, in_9, in_10, not_3_out);
  and and_8 (and_8_out, in_8, in_9, in_10, in_11);
  ExactlyOne xor_1 (
    .out(out_12), .in0(and_1_out), .in1(and_2_out), .in2(and_3_out), .in3(and_4_out), .in4(and_5_out),
    .in5(and_6_out), .in6(and_7_out), .in7(and_8_out));
endmodule

// DMUX 1x4
module DMUX (
  input  I,
  input  S0,
  input  S1,
  output IS0S1,
  output IS0S1_O1,
  output IS0S1_O2,
  output IS0S1_O3
);

  wire not_1_out, not_2_out;

  not not_1 (not_1_out, S0);
  not not_2 (not_2_out, S1);
  and and_1 (IS0S1, I, not_1_out, not_2_out);
  and and_2 (IS0S1_O1, I, not_1_out, S1);
  and and_3 (IS0S1_O2, I, S0, not_2_out);
  and and_4 (IS0S1_O3, I, S0, S1);
endmodule
